// Logisim project Assignment.circ as structural Verilog: 13 circuits, main circuit ALU
module ALU (
  input  [7:0] InputA,
  input  [7:0] InputB,
  input  [2:0] Shift_Length,
  input  [1:0] Operation_Select,
  output [7:0] Output
);

  wire [7:0] addition_1_output, logic_bitwise_and_1_output, register_right_logic_shift_1_output;

  Addition addition_1 (
    .A(InputA), .Add_Subtract_Control(1'b0), .B(InputB), .Output(addition_1_output));  // open: Carryout, Overflow
  Logic_bitwise_And logic_bitwise_and_1 (.A(InputA), .B(InputB), .Output(logic_bitwise_and_1_output));
  Register_right_logic_shift register_right_logic_shift_1 (
    .Input(InputA), .ShiftLen(Shift_Length), .Output(register_right_logic_shift_1_output));
  Multiplexer #(.select(2), .width(8), .enable("false")) multiplexer_1 (
    .in0(addition_1_output), .in1(logic_bitwise_and_1_output), .in2(register_right_logic_shift_1_output),
    .out(Output), .sel(Operation_Select));  // open: in3
endmodule

module Sub_HalfAdder (
  input  A,
  input  B,
  output S,
  output C
);

  xor xor_1 (S, A, B);
  and and_1 (C, A, B);
endmodule

module Increment (
  input  [7:0] Input,
  output [7:0] Output,
  output Carry
);

  wire sub_halfadder_1_c, sub_halfadder_2_c, sub_halfadder_3_c, sub_halfadder_4_c, sub_halfadder_5_c,
       sub_halfadder_6_c, sub_halfadder_7_c;

  Sub_HalfAdder sub_halfadder_1 (.A(1'b1), .B(Input[0]), .S(Output[0]), .C(sub_halfadder_1_c));
  Sub_HalfAdder sub_halfadder_2 (.A(sub_halfadder_1_c), .B(Input[1]), .S(Output[1]), .C(sub_halfadder_2_c));
  Sub_HalfAdder sub_halfadder_3 (.A(sub_halfadder_2_c), .B(Input[2]), .S(Output[2]), .C(sub_halfadder_3_c));
  Sub_HalfAdder sub_halfadder_4 (.A(sub_halfadder_3_c), .B(Input[3]), .S(Output[3]), .C(sub_halfadder_4_c));
  Sub_HalfAdder sub_halfadder_5 (.A(sub_halfadder_4_c), .B(Input[4]), .S(Output[4]), .C(sub_halfadder_5_c));
  Sub_HalfAdder sub_halfadder_6 (.A(sub_halfadder_5_c), .B(Input[5]), .S(Output[5]), .C(sub_halfadder_6_c));
  Sub_HalfAdder sub_halfadder_7 (.A(sub_halfadder_6_c), .B(Input[6]), .S(Output[6]), .C(sub_halfadder_7_c));
  Sub_HalfAdder sub_halfadder_8 (.A(sub_halfadder_7_c), .B(Input[7]), .S(Output[7]), .C(Carry));
endmodule

module Decrement (
  input  [7:0] Input,
  output [7:0] Output
);

  wire sub_fulladder_1_cout, sub_fulladder_2_cout, sub_fulladder_3_cout, sub_fulladder_4_cout,
       sub_fulladder_5_cout, sub_fulladder_6_cout, sub_fulladder_7_cout;

  Sub_FullAdder sub_fulladder_1 (.Cin(1'b1), .A(Input[0]), .B(1'b1), .Sum(Output[0]), .Cout(sub_fulladder_1_cout));
  Sub_FullAdder sub_fulladder_2 (
    .Cin(sub_fulladder_1_cout), .A(Input[1]), .B(1'b1), .Sum(Output[1]), .Cout(sub_fulladder_2_cout));
  Sub_FullAdder sub_fulladder_3 (
    .Cin(sub_fulladder_2_cout), .A(Input[2]), .B(1'b1), .Sum(Output[2]), .Cout(sub_fulladder_3_cout));
  Sub_FullAdder sub_fulladder_4 (
    .Cin(sub_fulladder_3_cout), .A(Input[3]), .B(1'b1), .Sum(Output[3]), .Cout(sub_fulladder_4_cout));
  Sub_FullAdder sub_fulladder_5 (
    .Cin(sub_fulladder_4_cout), .A(Input[4]), .B(1'b1), .Sum(Output[4]), .Cout(sub_fulladder_5_cout));
  Sub_FullAdder sub_fulladder_6 (
    .Cin(sub_fulladder_5_cout), .A(Input[5]), .B(1'b1), .Sum(Output[5]), .Cout(sub_fulladder_6_cout));
  Sub_FullAdder sub_fulladder_7 (
    .Cin(sub_fulladder_6_cout), .A(Input[6]), .B(1'b1), .Sum(Output[6]), .Cout(sub_fulladder_7_cout));
  Sub_FullAdder sub_fulladder_8 (.Cin(sub_fulladder_7_cout), .A(Input[7]), .B(1'b1), .Sum(Output[7]));  // open: Cout
endmodule

module Logic_bitwise_Not (
  input  [7:0] Input,
  output [7:0] Output
);

  not not_1 (Output[0], Input[0]);
  not not_2 (Output[1], Input[1]);
  not not_3 (Output[2], Input[2]);
  not not_4 (Output[3], Input[3]);
  not not_5 (Output[4], Input[4]);
  not not_6 (Output[5], Input[5]);
  not not_7 (Output[6], Input[6]);
  not not_8 (Output[7], Input[7]);
endmodule

module Logic_bitwise_And (
  input  [7:0] A,
  input  [7:0] B,
  output [7:0] Output
);

  and and_1 (Output[0], A[0], B[0]);
  and and_2 (Output[1], A[1], B[1]);
  and and_3 (Output[2], A[2], B[2]);
  and and_4 (Output[3], A[3], B[3]);
  and and_5 (Output[4], A[4], B[4]);
  and and_6 (Output[5], A[5], B[5]);
  and and_7 (Output[6], A[6], B[6]);
  and and_8 (Output[7], A[7], B[7]);
endmodule

module Logic_bitwise_Or (
  input  [7:0] A,
  input  [7:0] B,
  output [7:0] Output
);

  or or_1 (Output[0], A[0], B[0]);
  or or_2 (Output[1], A[1], B[1]);
  or or_3 (Output[2], A[2], B[2]);
  or or_4 (Output[3], A[3], B[3]);
  or or_5 (Output[4], A[4], B[4]);
  or or_6 (Output[5], A[5], B[5]);
  or or_7 (Output[6], A[6], B[6]);
  or or_8 (Output[7], A[7], B[7]);
endmodule

module Register_right_logic_shift (
  input  [7:0] Input,
  input  [2:0] ShiftLen,
  output [7:0] Output
);

  Shifter #(.shift("lr")) shifter_1 (.in(Input), .\dist (ShiftLen), .out(Output));
endmodule

module Register_left_logic_shift (
  input  [7:0] Input,
  input  [2:0] ShiftLen,
  output [7:0] Output
);

  Shifter shifter_1 (.in(Input), .\dist (ShiftLen), .out(Output));
endmodule

module Sub_FullAdder (
  input  Cin,
  input  A,
  input  B,
  output Sum,
  output Cout
);

  wire HA_1_c, HA_2_c, HA_2_s;

  Sub_HalfAdder HA_2 (.A(A), .B(B), .S(HA_2_s), .C(HA_2_c));
  Sub_HalfAdder HA_1 (.A(Cin), .B(HA_2_s), .S(Sum), .C(HA_1_c));
  or or_1 (Cout, HA_1_c, HA_2_c);
endmodule

module Addition (
  input  [7:0] A,
  input  Add_Subtract_Control,
  input  [7:0] B,
  output [7:0] Output,
  output Carryout,
  output Overflow
);

  wire and_1_out, and_2_out, not_1_out, not_2_out, not_3_out, sub_fulladder_1_cout, sub_fulladder_2_cout,
       sub_fulladder_3_cout, sub_fulladder_4_cout, sub_fulladder_5_cout, sub_fulladder_6_cout,
       sub_fulladder_7_cout, xor_1_out, xor_2_out, xor_3_out, xor_4_out, xor_5_out, xor_6_out, xor_7_out,
       xor_8_out;

  xor xor_1 (xor_1_out, Add_Subtract_Control, B[0]);
  xor xor_2 (xor_2_out, Add_Subtract_Control, B[1]);
  xor xor_3 (xor_3_out, Add_Subtract_Control, B[2]);
  xor xor_4 (xor_4_out, Add_Subtract_Control, B[3]);
  xor xor_5 (xor_5_out, Add_Subtract_Control, B[4]);
  xor xor_6 (xor_6_out, Add_Subtract_Control, B[5]);
  xor xor_7 (xor_7_out, Add_Subtract_Control, B[6]);
  xor xor_8 (xor_8_out, Add_Subtract_Control, B[7]);
  Sub_FullAdder sub_fulladder_1 (
    .Cin(A[0]), .A(Add_Subtract_Control), .B(xor_1_out), .Sum(Output[0]), .Cout(sub_fulladder_1_cout));
  Sub_FullAdder sub_fulladder_2 (
    .Cin(A[1]), .A(sub_fulladder_1_cout), .B(xor_2_out), .Sum(Output[1]), .Cout(sub_fulladder_2_cout));
  Sub_FullAdder sub_fulladder_3 (
    .Cin(A[2]), .A(sub_fulladder_2_cout), .B(xor_3_out), .Sum(Output[2]), .Cout(sub_fulladder_3_cout));
  Sub_FullAdder sub_fulladder_4 (
    .Cin(A[3]), .A(sub_fulladder_3_cout), .B(xor_4_out), .Sum(Output[3]), .Cout(sub_fulladder_4_cout));
  Sub_FullAdder sub_fulladder_5 (
    .Cin(A[4]), .A(sub_fulladder_4_cout), .B(xor_5_out), .Sum(Output[4]), .Cout(sub_fulladder_5_cout));
  Sub_FullAdder sub_fulladder_6 (
    .Cin(A[5]), .A(sub_fulladder_5_cout), .B(xor_6_out), .Sum(Output[5]), .Cout(sub_fulladder_6_cout));
  Sub_FullAdder sub_fulladder_7 (
    .Cin(A[6]), .A(sub_fulladder_6_cout), .B(xor_7_out), .Sum(Output[6]), .Cout(sub_fulladder_7_cout));
  Sub_FullAdder sub_fulladder_8 (.Cin(A[7]), .A(sub_fulladder_7_cout), .B(xor_8_out), .Sum(Output[7]), .Cout(Carryout));
  not not_1 (not_1_out, A[7]);
  not not_2 (not_2_out, xor_8_out);
  and and_1 (and_1_out, Output[7], not_1_out, not_2_out);
  not not_3 (not_3_out, Output[7]);
  and and_2 (and_2_out, not_3_out, A[7], xor_8_out);
  or or_1 (Overflow, and_1_out, and_2_out);
endmodule

module Sub_LessGreatEqual (
  input  Eq_In,
  input  A,
  input  B,
  output A___B,
  output A___B_2,
  output A___B_3
);

  wire and_3_out, and_4_out, nor_1_out, not_1_out, not_2_out, not_3_out, not_4_out, or_1_out;

  not not_1 (not_1_out, B);
  and and_1 (A___B, A, Eq_In, not_1_out);
  not not_2 (not_2_out, A);
  and and_2 (A___B_2, not_2_out, Eq_In, B);
  not not_3 (not_3_out, A);
  not not_4 (not_4_out, B);
  nor nor_1 (nor_1_out, A___B, A___B_2);
  and and_3 (and_3_out, A, B);
  and and_4 (and_4_out, not_3_out, not_4_out);
  or or_1 (or_1_out, and_3_out, and_4_out);
  and and_5 (A___B_3, Eq_In, nor_1_out, or_1_out);
endmodule

module Comparison (
  input  [7:0] A,
  input  [7:0] B,
  output A___B,
  output A___B_2,
  output A___B_3
);

  wire sub_lessgreatequal_1_a___b, sub_lessgreatequal_1_a___b_2, sub_lessgreatequal_1_a___b_3,
       sub_lessgreatequal_2_a___b, sub_lessgreatequal_2_a___b_2, sub_lessgreatequal_2_a___b_3,
       sub_lessgreatequal_3_a___b, sub_lessgreatequal_3_a___b_2, sub_lessgreatequal_3_a___b_3,
       sub_lessgreatequal_4_a___b, sub_lessgreatequal_4_a___b_2, sub_lessgreatequal_4_a___b_3,
       sub_lessgreatequal_5_a___b, sub_lessgreatequal_5_a___b_2, sub_lessgreatequal_5_a___b_3,
       sub_lessgreatequal_6_a___b, sub_lessgreatequal_6_a___b_2, sub_lessgreatequal_6_a___b_3,
       sub_lessgreatequal_7_a___b, sub_lessgreatequal_7_a___b_2, sub_lessgreatequal_7_a___b_3,
       sub_lessgreatequal_8_a___b, sub_lessgreatequal_8_a___b_2;

  Sub_LessGreatEqual sub_lessgreatequal_1 (
    .A(A[7]), .B(B[7]), .Eq_In(1'b1), .A___B(sub_lessgreatequal_1_a___b),
    .A___B_2(sub_lessgreatequal_1_a___b_2), .A___B_3(sub_lessgreatequal_1_a___b_3));
  Sub_LessGreatEqual sub_lessgreatequal_2 (
    .A(A[6]), .B(B[6]), .Eq_In(sub_lessgreatequal_1_a___b_3), .A___B(sub_lessgreatequal_2_a___b),
    .A___B_2(sub_lessgreatequal_2_a___b_2), .A___B_3(sub_lessgreatequal_2_a___b_3));
  Sub_LessGreatEqual sub_lessgreatequal_3 (
    .A(A[5]), .B(B[5]), .Eq_In(sub_lessgreatequal_2_a___b_3), .A___B(sub_lessgreatequal_3_a___b),
    .A___B_2(sub_lessgreatequal_3_a___b_2), .A___B_3(sub_lessgreatequal_3_a___b_3));
  Sub_LessGreatEqual sub_lessgreatequal_4 (
    .A(A[4]), .B(B[4]), .Eq_In(sub_lessgreatequal_3_a___b_3), .A___B(sub_lessgreatequal_4_a___b),
    .A___B_2(sub_lessgreatequal_4_a___b_2), .A___B_3(sub_lessgreatequal_4_a___b_3));
  Sub_LessGreatEqual sub_lessgreatequal_5 (
    .A(A[3]), .B(B[3]), .Eq_In(sub_lessgreatequal_4_a___b_3), .A___B(sub_lessgreatequal_5_a___b),
    .A___B_2(sub_lessgreatequal_5_a___b_2), .A___B_3(sub_lessgreatequal_5_a___b_3));
  Sub_LessGreatEqual sub_lessgreatequal_6 (
    .A(A[2]), .B(B[2]), .Eq_In(sub_lessgreatequal_5_a___b_3), .A___B(sub_lessgreatequal_6_a___b),
    .A___B_2(sub_lessgreatequal_6_a___b_2), .A___B_3(sub_lessgreatequal_6_a___b_3));
  Sub_LessGreatEqual sub_lessgreatequal_7 (
    .A(A[1]), .B(B[1]), .Eq_In(sub_lessgreatequal_6_a___b_3), .A___B(sub_lessgreatequal_7_a___b),
    .A___B_2(sub_lessgreatequal_7_a___b_2), .A___B_3(sub_lessgreatequal_7_a___b_3));
  Sub_LessGreatEqual sub_lessgreatequal_8 (
    .A(A[0]), .B(B[0]), .Eq_In(sub_lessgreatequal_7_a___b_3), .A___B(sub_lessgreatequal_8_a___b),
    .A___B_2(sub_lessgreatequal_8_a___b_2), .A___B_3(A___B_3));
  or or_1 (A___B, sub_lessgreatequal_1_a___b, sub_lessgreatequal_2_a___b, sub_lessgreatequal_3_a___b, sub_lessgreatequal_4_a___b, sub_lessgreatequal_5_a___b, sub_lessgreatequal_6_a___b, sub_lessgreatequal_7_a___b, sub_lessgreatequal_8_a___b);
  or or_2 (A___B_2, sub_lessgreatequal_1_a___b_2, sub_lessgreatequal_2_a___b_2, sub_lessgreatequal_3_a___b_2, sub_lessgreatequal_4_a___b_2, sub_lessgreatequal_5_a___b_2, sub_lessgreatequal_6_a___b_2, sub_lessgreatequal_7_a___b_2, sub_lessgreatequal_8_a___b_2);
endmodule
